// Digital circuit 5bit_CPU.dig as structural Verilog
module _5bit_CPU (
  input  [3:0] RA2__3_0,
  input  [3:0] WR__3_0,
  input  [16:0] WRD__16_0,
  input  WE,
  input  CLK,
  input  PC_EN,
  output [16:0] RD2__16_0,
  output [2:0] R2__2_0,
  output [2:0] R1__2_0,
  output [2:0] WR__2_0,
  output [4:0] A__4_0,
  output [4:0] B__4_0,
  output [4:0] R__4_0,
  output [3:0] JMP_ADDR__3_0,
  output CF
);

  wire _4bit_pc_adder_1_p2, _5bit_alu_1_p3, CPU_CLK, Imm_Sel, JMP_Sel, Op, REG_EN;
  wire [1:0] Imm_val;
  wire [3:0] _4bit_pc_adder_1_p1, _10x17_ram_1_p7, multiplexer_1_out;
  wire [4:0] _5bit_reg_set_1_p6, XX;

  Multiplexer #(.Bits(4)) multiplexer_1 (
    .sel(JMP_Sel), .in_0(_4bit_pc_adder_1_p1), .in_1(JMP_ADDR__3_0), .out(multiplexer_1_out));
  // _4bit_PC_Adder _4bit_pc_adder_1: pin names not known; wires that end beside it: _4bit_pc_adder_1_p1, _4bit_pc_adder_1_p2
  // _4bit_PC _4bit_pc_1: pin names not known; wires that end beside it: multiplexer_1_out, CPU_CLK, _4bit_pc_adder_1_p2
  and and_1 (CPU_CLK, PC_EN, CLK);
  // _10x17_RAM _10x17_ram_1: pin names not known; wires that end beside it: _4bit_pc_adder_1_p2, RA2__3_0, WR__3_0, WRD__16_0, WE, CLK, {_10x17_ram_1_p7, JMP_ADDR__3_0, R2__2_0[1:0], Imm_val, XX}, RD2__16_0
  // _5bit_CU _5bit_cu_1: pin names not known; wires that end beside it: _10x17_ram_1_p7, CF, Op, REG_EN, Imm_Sel, JMP_Sel
  // _5bit_Reg_Set _5bit_reg_set_1: pin names not known; wires that end beside it: JMP_ADDR__3_0[3:1], CPU_CLK, JMP_ADDR__3_0[3:1], A__4_0, {JMP_ADDR__3_0[0], R2__2_0[1:0]}, _5bit_reg_set_1_p6, REG_EN, R__4_0
  // _5bit_ALU _5bit_alu_1: pin names not known; wires that end beside it: Op, A__4_0, _5bit_alu_1_p3, B__4_0, R__4_0
  Multiplexer #(.Bits(5)) multiplexer_2 (
    .sel(Imm_Sel), .in_0(_5bit_reg_set_1_p6), .in_1({JMP_ADDR__3_0[0], R2__2_0[1:0], Imm_val}), .out(B__4_0));
  // _1bit_Reg _1bit_reg_1: pin names not known; wires that end beside it: _5bit_alu_1_p3, 1'b1, CLK, CF

  assign R1__2_0 = JMP_ADDR__3_0[3:1];
  assign R2__2_0[2] = JMP_ADDR__3_0[0];
  assign WR__2_0 = JMP_ADDR__3_0[3:1];

  // Other names for the same wires on the sheet: XX[6:5] = Imm_val; Imm_val[4:2] = {JMP_ADDR__3_0[0], R2__2_0[1:0]};
  //   R2[2:0] = {JMP_ADDR__3_0[0], R2__2_0[1:0]}; JMP_ADDR[3:0] = JMP_ADDR__3_0; R1[2:0] = JMP_ADDR__3_0[3:1];
  //   A[4:0] = A__4_0; B[4:0] = B__4_0; RD2[16:0] = RD2__16_0

  // Notes on the sheet:
  //   Register Mode (Type of Op=00) = 2bit(Type of Op) + 2bit (Op) + 3bit (Reg1) + 3bit (Reg2) + 7bit (Don't care) 
  //   Immediate Mode (Type of Op=01) = 2bit(Type of Op) + 2bit (Op) + 3bit (Reg1) + 5bit (Imm Val) + 5bit (Don't care)
  //   Jump Mode (Type of Op=10) = 2bit(Type of Op) + 2bit (Op) + 4bit (Address) + 9bit (Don't care)
  //   Add (Op = 00), ROL (Op = 01), AND (Op = 10)
  //   JMP (Op = 00), JC (Op = 01)
endmodule
